// Logisim project lab2.circ as structural Verilog: 10 circuits, main circuit 四位二进制可逆计数器
module CLA_4Bits (
  input  A3,
  input  B3,
  input  A2,
  input  B2,
  input  A1,
  input  B1,
  input  A0,
  input  B0,
  input  C0,
  output C4,
  output S3,
  output S2,
  output S1,
  output S0
);

  wire and_1_out, and_2_out, and_3_out, and_4_out, and_5_out, and_6_out, and_7_out, and_8_out, and_9_out,
       and_10_out, C1_out, C2_out, C3_out, G0_out, G1_out, G2_out, G3_out, P0_out, P1_out, P2_out, P3_out;

  and G3 (G3_out, A3, B3);
  xor P3 (P3_out, A3, B3);
  and G2 (G2_out, A2, B2);
  xor P2 (P2_out, A2, B2);
  and G1 (G1_out, A1, B1);
  xor P1 (P1_out, A1, B1);
  and G0 (G0_out, A0, B0);
  xor P0 (P0_out, A0, B0);
  and and_1 (and_1_out, P3_out, P2_out, G1_out);
  and and_2 (and_2_out, P2_out, G1_out);
  and and_3 (and_3_out, P1_out, G0_out);
  and and_4 (and_4_out, P1_out, P0_out, C0);
  and and_5 (and_5_out, P0_out, C0);
  xor xor_1 (S0, P0_out, C0);
  and and_6 (and_6_out, P3_out, P2_out, P1_out, P0_out, C0);
  and and_7 (and_7_out, P3_out, P2_out, P1_out, G0_out);
  and and_8 (and_8_out, P2_out, P1_out, P0_out, C0);
  and and_9 (and_9_out, P2_out, P1_out, G0_out);
  or C2 (C2_out, G1_out, and_3_out, and_4_out);
  or C1 (C1_out, G0_out, and_5_out);
  and and_10 (and_10_out, P3_out, G2_out);
  or C3 (C3_out, and_8_out, and_9_out, G2_out, and_2_out);
  xor xor_2 (S2, P2_out, C2_out);
  xor xor_3 (S1, P1_out, C1_out);
  or or_1 (C4, and_6_out, and_7_out, and_1_out, and_10_out, G3_out);
  xor xor_4 (S3, P3_out, C3_out);

  // Notes on the sheet:
  //   C0: pull=down
endmodule

module \四位二进制可逆计数器  (
  input  CP_U,
  input  CP_D,
  input  nLD,
  input  A,
  input  CLR,
  input  B,
  input  C,
  input  D,
  output Q_A,
  output Q_B,
  output Q_C,
  output Q_D
);

  wire and_1_out, and_2_out, and_3_out, and_4_out, and_5_out, and_6_out, and_7_out, and_8_out, and_9_out,
       and_10_out, and_11_out, and_12_out, and_13_out, and_14_out, d_ff_1_qn, d_ff_2_qn, d_ff_3_qn,
       d_ff_4_qn, not_1_out, not_2_out, not_3_out, or_1_out, or_2_out, or_3_out, or_4_out, or_5_out,
       or_6_out, or_7_out, or_8_out;

  not not_1 (not_1_out, CP_U);
  not not_2 (not_2_out, CP_D);
  not not_3 (not_3_out, nLD);
  or or_1 (or_1_out, not_1_out, not_2_out);
  and and_1 (and_1_out, not_3_out, ~CLR, A);  // AND_Gate
  and and_2 (and_2_out, Q_A, not_1_out);
  and and_3 (and_3_out, d_ff_1_qn, not_2_out);
  and and_4 (and_4_out, not_3_out, ~CLR, B);  // AND_Gate
  and and_5 (and_5_out, Q_A, Q_B, not_1_out);
  and and_6 (and_6_out, d_ff_1_qn, d_ff_2_qn, not_2_out);
  and and_7 (and_7_out, not_3_out, ~CLR, C);  // AND_Gate
  and and_8 (and_8_out, Q_A, Q_B, Q_C, not_1_out);
  and and_9 (and_9_out, d_ff_1_qn, d_ff_2_qn, d_ff_3_qn, not_2_out);
  and and_10 (and_10_out, not_3_out, ~CLR, D);  // AND_Gate
  and and_11 (and_11_out, not_3_out, ~and_1_out);  // AND_Gate
  or or_2 (or_2_out, and_2_out, and_3_out);
  and and_12 (and_12_out, not_3_out, ~and_4_out);  // AND_Gate
  or or_3 (or_3_out, and_5_out, and_6_out);
  and and_13 (and_13_out, not_3_out, ~and_7_out);  // AND_Gate
  or or_4 (or_4_out, and_8_out, and_9_out);
  and and_14 (and_14_out, not_3_out, ~and_10_out);  // AND_Gate
  D_Flip_Flop #(.trigger("falling")) d_ff_1 (
    .clk(or_1_out), .D(d_ff_1_qn), .Q(Q_A), .Qn(d_ff_1_qn), .preset(and_1_out), .reset(or_5_out));
  or or_5 (or_5_out, and_11_out, CLR);
  D_Flip_Flop #(.trigger("falling")) d_ff_2 (
    .clk(or_2_out), .D(d_ff_2_qn), .Q(Q_B), .Qn(d_ff_2_qn), .preset(and_4_out), .reset(or_6_out));
  or or_6 (or_6_out, and_12_out, CLR);
  D_Flip_Flop #(.trigger("falling")) d_ff_3 (
    .clk(or_3_out), .D(d_ff_3_qn), .Q(Q_C), .Qn(d_ff_3_qn), .preset(and_7_out), .reset(or_7_out));
  or or_7 (or_7_out, and_13_out, CLR);
  D_Flip_Flop #(.trigger("falling")) d_ff_4 (
    .clk(or_4_out), .D(d_ff_4_qn), .Q(Q_D), .Qn(d_ff_4_qn), .preset(and_10_out), .reset(or_8_out));
  or or_8 (or_8_out, and_14_out, CLR);
endmodule

module \四位二进制可逆计数器测试电路  (
  input  in_1,
  input  in_2,
  input  in_3,
  input  in_4,
  input  in_5,
  input  in_6,
  output out_7,
  output out_8,
  output out_9,
  output out_10
);

  wire button_1_out, button_2_out;

  Button button_1 (.out(button_1_out));
  Button button_2 (.out(button_2_out));
  \四位二进制可逆计数器  \u_四位二进制可逆计数器_1  (
    .CP_D(button_2_out), .nLD(in_6), .A(in_5), .CLR(in_1), .B(in_4), .C(in_3), .D(in_2), .Q_A(out_10),
    .Q_B(out_9), .Q_C(out_8), .Q_D(out_7), .CP_U(button_1_out));
endmodule

module \二进制转8421码电路  (
  input  Q_D,
  input  Q_C,
  input  Q_B,
  input  Q_A,
  output H_3,
  output H_2,
  output H_1,
  output H_0,
  output L_3,
  output L_2,
  output L_1,
  output L_0
);

  wire or_1_out;

  or or_1 (or_1_out, Q_C, Q_B);
  CLA_4Bits cla_4bits_1 (
    .B1(Q_B), .S2(L_2), .A3(1'b0), .S1(L_1), .C0(1'b0), .B3(Q_D), .S3(L_3), .A2(H_0), .A1(H_0), .S0(L_0),
    .B2(Q_C), .A0(1'b0), .B0(Q_A));  // open: C4
  and and_1 (H_0, Q_D, or_1_out);

  assign H_1 = 1'b0;
  assign H_2 = 1'b0;
  assign H_3 = 1'b0;
endmodule

module \二进制转8421码测试电路  (
  input  in_1,
  input  in_2,
  input  in_3,
  input  in_4,
  output out_5,
  output out_6,
  output out_7,
  output out_8,
  output out_9,
  output out_10,
  output out_11,
  output out_12
);

  \二进制转8421码电路  \u_二进制转8421码电路_1  (
    .Q_D(in_1), .Q_C(in_2), .Q_B(in_3), .Q_A(in_4), .H_3(out_5), .H_2(out_6), .H_1(out_7), .H_0(out_8),
    .L_3(out_9), .L_2(out_10), .L_1(out_11), .L_0(out_12));
endmodule

module \显示电路  (
  input  A,
  input  B,
  input  C,
  input  D,
  output out_5,
  output out_6,
  output out_7,
  output out_8,
  output out_9,
  output out_10,
  output out_11
);

  wire A_nBC_out, AB_out, AC_out, B_nC_out, nA_nB_nC_out, nA_nB_out, nA_nC_nD_out, nAB_out, nAC_out, nBC_out,
       not_1_out, not_2_out, not_3_out, not_4_out;

  not not_1 (not_1_out, A);
  not not_2 (not_2_out, B);
  not not_3 (not_3_out, C);
  not not_4 (not_4_out, D);
  and AB (AB_out, A, B);
  and nAB (nAB_out, not_1_out, B);
  and nA_nB (nA_nB_out, not_1_out, not_2_out);
  and AC (AC_out, A, C);
  and nAC (nAC_out, not_1_out, C);
  and B_nC (B_nC_out, B, not_3_out);
  and nBC (nBC_out, not_2_out, C);
  and A_nBC (A_nBC_out, A, not_2_out, C);
  and nA_nB_nC (nA_nB_nC_out, not_1_out, not_2_out, not_3_out);
  and nA_nC_nD (nA_nC_nD_out, not_1_out, not_3_out, not_4_out);
  or or_1 (out_5, AB_out, AC_out, nA_nC_nD_out, D);
  or or_2 (out_6, AB_out, nA_nB_out, ~C);  // OR_Gate
  or or_3 (out_7, A, not_2_out, C, D);
  or or_4 (out_8, nAB_out, B_nC_out, A_nBC_out, nA_nB_nC_out);
  or or_5 (out_9, nAB_out, nA_nB_nC_out);
  or or_6 (out_10, nA_nB_out, nAC_out, nBC_out, D);
  or or_7 (out_11, nAB_out, B_nC_out, nBC_out, D);
endmodule

module \显示电路测试电路  (
  input  in_1,
  input  in_2,
  input  in_3,
  input  in_4
);

  wire \显示电路_1_out_5 , \显示电路_1_out_6 , \显示电路_1_out_7 , \显示电路_1_out_8 , \显示电路_1_out_9 , \显示电路_1_out_10 ,
       \显示电路_1_out_11 ;

  \显示电路  \u_显示电路_1  (
    .A(in_1), .B(in_2), .C(in_3), .D(in_4), .out_5(\显示电路_1_out_5 ), .out_6(\显示电路_1_out_6 ),
    .out_7(\显示电路_1_out_7 ), .out_8(\显示电路_1_out_8 ), .out_9(\显示电路_1_out_9 ), .out_10(\显示电路_1_out_10 ),
    .out_11(\显示电路_1_out_11 ));
  _7_Segment_Display u_7_segment_display_1 (
    .g(\显示电路_1_out_11 ), .f(\显示电路_1_out_10 ), .a(\显示电路_1_out_5 ), .b(\显示电路_1_out_6 ), .e(\显示电路_1_out_9 ),
    .d(\显示电路_1_out_8 ), .c(\显示电路_1_out_7 ), .dp(1'b0));
endmodule

module \报警电路  (
  input  CP_prime__U,
  input  in_2,
  input  CP_prime__D,
  input  in_4,
  input  in_5,
  input  in_6,
  input  in_7,
  input  in_8,
  output WARN,
  output out_10,
  output out_11,
  output out_12,
  output out_13
);

  wire and_2_out, nand_1_out, nand_2_out, or_1_out;

  or or_1 (or_1_out, out_13, out_12, out_11, out_10);
  and and_1 (WARN, CP_prime__U, and_2_out);
  and and_2 (and_2_out, out_13, out_12, out_11, out_10);
  nand nand_1 (nand_1_out, ~and_2_out, CP_prime__U);  // NAND_Gate
  nand nand_2 (nand_2_out, or_1_out, CP_prime__D);
  \四位二进制可逆计数器  \u_四位二进制可逆计数器_1  (
    .CP_D(nand_2_out), .nLD(in_8), .A(in_7), .CLR(in_2), .B(in_6), .C(in_5), .D(in_4), .Q_A(out_13),
    .Q_B(out_12), .Q_C(out_11), .Q_D(out_10), .CP_U(nand_1_out));
endmodule

module \小型实验室门禁系统  (
  input  in_1,
  input  in_2,
  input  in_3,
  output out_4,
  output out_5,
  output out_6,
  output out_7,
  output out_8,
  output out_9,
  output out_10,
  output out_11,
  output out_12,
  output out_13,
  output out_14,
  output out_15,
  output out_16,
  output out_17,
  output out_18
);

  wire \二进制转8421码电路_1_h_0 , \二进制转8421码电路_1_h_1 , \二进制转8421码电路_1_h_2 , \二进制转8421码电路_1_h_3 ,
       \二进制转8421码电路_1_l_0 , \二进制转8421码电路_1_l_1 , \二进制转8421码电路_1_l_2 , \二进制转8421码电路_1_l_3 , \报警电路_1_out_10 ,
       \报警电路_1_out_11 , \报警电路_1_out_12 , \报警电路_1_out_13 ;

  \报警电路  \u_报警电路_1  (
    .CP_prime__U(in_1), .in_2(in_2), .CP_prime__D(in_3), .WARN(out_18), .out_10(\报警电路_1_out_10 ),
    .out_11(\报警电路_1_out_11 ), .out_12(\报警电路_1_out_12 ), .out_13(\报警电路_1_out_13 ), .in_4(1'b0), .in_5(1'b0),
    .in_6(1'b0), .in_7(1'b0), .in_8(1'b1));
  \二进制转8421码电路  \u_二进制转8421码电路_1  (
    .Q_D(\报警电路_1_out_10 ), .Q_C(\报警电路_1_out_11 ), .Q_B(\报警电路_1_out_12 ), .Q_A(\报警电路_1_out_13 ),
    .H_3(\二进制转8421码电路_1_h_3 ), .H_2(\二进制转8421码电路_1_h_2 ), .H_1(\二进制转8421码电路_1_h_1 ),
    .H_0(\二进制转8421码电路_1_h_0 ), .L_3(\二进制转8421码电路_1_l_3 ), .L_2(\二进制转8421码电路_1_l_2 ),
    .L_1(\二进制转8421码电路_1_l_1 ), .L_0(\二进制转8421码电路_1_l_0 ));
  \显示电路  \u_显示电路_1  (
    .A(\二进制转8421码电路_1_h_0 ), .B(\二进制转8421码电路_1_h_1 ), .C(\二进制转8421码电路_1_h_2 ), .D(\二进制转8421码电路_1_h_3 ),
    .out_5(out_4), .out_6(out_5), .out_7(out_6), .out_8(out_7), .out_9(out_8), .out_10(out_9), .out_11(out_10));
  \显示电路  \u_显示电路_2  (
    .A(\二进制转8421码电路_1_l_0 ), .B(\二进制转8421码电路_1_l_1 ), .C(\二进制转8421码电路_1_l_2 ), .D(\二进制转8421码电路_1_l_3 ),
    .out_5(out_11), .out_6(out_12), .out_7(out_13), .out_8(out_14), .out_9(out_15), .out_10(out_16),
    .out_11(out_17));
endmodule

module \小型门禁系统测试电路  (
);

  wire button_1_out, button_2_out, button_3_out, \小型实验室门禁系统_1_out_4 , \小型实验室门禁系统_1_out_5 ,
       \小型实验室门禁系统_1_out_6 , \小型实验室门禁系统_1_out_7 , \小型实验室门禁系统_1_out_8 , \小型实验室门禁系统_1_out_9 ,
       \小型实验室门禁系统_1_out_10 , \小型实验室门禁系统_1_out_11 , \小型实验室门禁系统_1_out_12 , \小型实验室门禁系统_1_out_13 ,
       \小型实验室门禁系统_1_out_14 , \小型实验室门禁系统_1_out_15 , \小型实验室门禁系统_1_out_16 , \小型实验室门禁系统_1_out_17 ,
       \小型实验室门禁系统_1_out_18 ;

  _7_Segment_Display u_7_segment_display_1 (
    .g(\小型实验室门禁系统_1_out_10 ), .f(\小型实验室门禁系统_1_out_9 ), .a(\小型实验室门禁系统_1_out_4 ), .b(\小型实验室门禁系统_1_out_5 ),
    .e(\小型实验室门禁系统_1_out_8 ), .d(\小型实验室门禁系统_1_out_7 ), .c(\小型实验室门禁系统_1_out_6 ), .dp(1'b0));
  \小型实验室门禁系统  \u_小型实验室门禁系统_1  (
    .in_1(button_1_out), .in_2(button_2_out), .in_3(button_3_out), .out_4(\小型实验室门禁系统_1_out_4 ),
    .out_5(\小型实验室门禁系统_1_out_5 ), .out_6(\小型实验室门禁系统_1_out_6 ), .out_7(\小型实验室门禁系统_1_out_7 ),
    .out_8(\小型实验室门禁系统_1_out_8 ), .out_9(\小型实验室门禁系统_1_out_9 ), .out_10(\小型实验室门禁系统_1_out_10 ),
    .out_11(\小型实验室门禁系统_1_out_11 ), .out_12(\小型实验室门禁系统_1_out_12 ), .out_13(\小型实验室门禁系统_1_out_13 ),
    .out_14(\小型实验室门禁系统_1_out_14 ), .out_15(\小型实验室门禁系统_1_out_15 ), .out_16(\小型实验室门禁系统_1_out_16 ),
    .out_17(\小型实验室门禁系统_1_out_17 ), .out_18(\小型实验室门禁系统_1_out_18 ));
  Button button_1 (.out(button_1_out));
  Button button_2 (.out(button_2_out));
  Button button_3 (.out(button_3_out));
  _7_Segment_Display u_7_segment_display_2 (
    .g(\小型实验室门禁系统_1_out_17 ), .f(\小型实验室门禁系统_1_out_16 ), .a(\小型实验室门禁系统_1_out_11 ), .b(\小型实验室门禁系统_1_out_12 ),
    .e(\小型实验室门禁系统_1_out_15 ), .d(\小型实验室门禁系统_1_out_14 ), .c(\小型实验室门禁系统_1_out_13 ), .dp(1'b0));
  // Buzzer buzzer_1: pin names not known; wires that end beside it: \小型实验室门禁系统_1_out_18 
  LED led_1 (.in(\小型实验室门禁系统_1_out_18 ));
endmodule
