// Logisim project lab4.circ as structural Verilog
module \四位除法器  (
  input  [3:0] n2,
  input  [3:0] d,
  output [3:0] quot,
  output [3:0] rem
);

  wire [2:0] divbodyunit_1_out_4, divbodyunit_2_out_4, divbodyunit_3_out_4;
  wire [3:0] divbodyunit_1_out_5, divbodyunit_2_out_5, divbodyunit_3_out_5;

  DivBodyUnit divbodyunit_1 (
    .in_1(n2[2:0]), .in_2({3'b000, n2[3]}), .in_3(d), .out_4(divbodyunit_1_out_4), .out_5(divbodyunit_1_out_5));
  DivBodyUnit divbodyunit_2 (
    .in_1(divbodyunit_1_out_4), .in_2(divbodyunit_1_out_5), .in_3(d), .out_4(divbodyunit_2_out_4),
    .out_5(divbodyunit_2_out_5));
  DivBodyUnit divbodyunit_3 (
    .in_1(divbodyunit_2_out_4), .in_2(divbodyunit_2_out_5), .in_3(d), .out_4(divbodyunit_3_out_4),
    .out_5(divbodyunit_3_out_5));
  DivFoot divfoot_1 (.in_1(divbodyunit_3_out_4), .in_2(divbodyunit_3_out_5), .in_3(d), .out_4(quot), .out_5(rem));
endmodule

module \四位除法器测试电路  (
  input  [3:0] in_1,
  input  [3:0] in_2,
  output [3:0] out_3,
  output [3:0] out_4
);

  // Probe on in_1
  // Probe on in_2
  \四位除法器  \u_四位除法器_1  (.n2(in_1), .d(in_2), .quot(out_3), .rem(out_4));
  // Probe on out_3
  // Probe on out_4
endmodule

module DivBodyUnit (
  input  [2:0] in_1,
  input  [3:0] in_2,
  input  [3:0] in_3,
  output [2:0] out_4,
  output [3:0] out_5
);

  wire comparator_1_lt;
  wire [3:0] subtractor_1_out;
  wire [3:3] multiplexer_1_out;

  Subtractor #(.width(4)) subtractor_1 (.a(in_2), .b(in_3), .out(subtractor_1_out));  // open: bin, bout
  Comparator #(.width(4), .mode("unsigned")) comparator_1 (.a(in_2), .b(in_3), .lt(comparator_1_lt));  // open: gt, eq
  Multiplexer #(.width(4), .enable("false")) multiplexer_1 (
    .in0(in_2), .in1(subtractor_1_out), .out({multiplexer_1_out[3], out_5[3:1]}), .sel(out_4[0]));
  not not_1 (out_4[0], comparator_1_lt);

  assign out_4[2:1] = in_1[1:0];
  assign out_5[0] = in_1[2];
endmodule

module DivFoot (
  input  [2:0] in_1,
  input  [3:0] in_2,
  input  [3:0] in_3,
  output [3:0] out_4,
  output [3:0] out_5
);

  wire comparator_1_lt;
  wire [3:0] subtractor_1_out;

  Subtractor #(.width(4)) subtractor_1 (.a(in_2), .b(in_3), .out(subtractor_1_out));  // open: bin, bout
  Comparator #(.width(4), .mode("unsigned")) comparator_1 (.a(in_2), .b(in_3), .lt(comparator_1_lt));  // open: gt, eq
  Multiplexer #(.width(4), .enable("false")) multiplexer_1 (
    .in0(in_2), .in1(subtractor_1_out), .out(out_5), .sel(out_4[0]));
  not not_1 (out_4[0], comparator_1_lt);

  assign out_4[3:1] = in_1;
endmodule
