// Logisim project lab5.circ as structural Verilog: 19 circuits, main circuit main
module main (
  input  Set,
  input  Clr,
  input  Adj1,
  input  Adj0,
  output out_5
);

  wire and_1_out, and_2_out, and_3_out, and_4_out, CP_out, CPd_out, CPu_out, n12new_1_q0a, n12new_1_q0b,
       n12new_1_q0c, n12new_1_q0d, n12new_1_q1a, n12new_1_q1b, n12new_1_q1c, n12new_1_q1d, not_1_out,
       not_2_out, or_1_out, or_2_out, or_3_out, time_report_1_out_13, \六十进制计数器_1_nqcc , \六十进制计数器_1_q0a ,
       \六十进制计数器_1_q0b , \六十进制计数器_1_q0c , \六十进制计数器_1_q0d , \六十进制计数器_1_q1a , \六十进制计数器_1_q1b , \六十进制计数器_1_q1c ,
       \六十进制计数器_1_q1d , \六十进制计数器_2_nqcc , \六十进制计数器_2_q0a , \六十进制计数器_2_q0b , \六十进制计数器_2_q0c , \六十进制计数器_2_q0d ,
       \六十进制计数器_2_q1a , \六十进制计数器_2_q1b , \六十进制计数器_2_q1c , \六十进制计数器_2_q1d ;
  wire [3:0] ledbase_1_out_5, ledbase_2_out_5, ledbase_3_out_5, ledbase_4_out_5, ledbase_5_out_5,
       ledbase_6_out_5;
  wire [4:0] am_pm_1_out_3, am_pm_1_out_4, am_pm_1_out_5, am_pm_1_out_6;

  Button CPu (.out(CPu_out));
  Button CPd (.out(CPd_out));
  not not_1 (not_1_out, Set);
  or or_1 (or_1_out, Adj1, Adj0);
  and and_1 (and_1_out, Adj1, CPu_out);
  and and_2 (and_2_out, ~or_1_out, \六十进制计数器_1_nqcc );  // AND_Gate
  DotMatrix #(.matrixcols(4), .matrixrows(5)) dotmatrix_1 (
    .col0(am_pm_1_out_3), .col1(am_pm_1_out_4), .col2(am_pm_1_out_5), .col3(am_pm_1_out_6));
  AM_PM am_pm_1 (
    .AMPM(not_2_out), .TT(not_1_out), .out_3(am_pm_1_out_3), .out_4(am_pm_1_out_4), .out_5(am_pm_1_out_5),
    .out_6(am_pm_1_out_6));
  not not_2 (not_2_out, out_5);
  or or_2 (or_2_out, and_2_out, and_1_out);
  Hex_Digit_Display hex_digit_display_1 (.value(ledbase_1_out_5));  // open: dp
  LEDBase ledbase_1 (
    .in_1(n12new_1_q1a), .in_2(n12new_1_q1b), .in_3(n12new_1_q1c), .in_4(n12new_1_q1d),
    .out_5(ledbase_1_out_5));
  Hex_Digit_Display hex_digit_display_2 (.value(ledbase_2_out_5));  // open: dp
  LEDBase ledbase_2 (
    .in_1(n12new_1_q0a), .in_2(n12new_1_q0b), .in_3(n12new_1_q0c), .in_4(n12new_1_q0d),
    .out_5(ledbase_2_out_5));
  _12new u_12new_1 (
    .Set(Set), .Clr(Clr), .Cpu(or_2_out), .Adj(Adj1), .Cpd(CPd_out), .Q1d(n12new_1_q1d), .Q1c(n12new_1_q1c),
    .Q1b(n12new_1_q1b), .Q1a(n12new_1_q1a), .out_11(out_5), .Q0d(n12new_1_q0d), .Q0c(n12new_1_q0c),
    .Q0b(n12new_1_q0b), .Q0a(n12new_1_q0a));  // open: out_6
  and and_3 (and_3_out, ~or_1_out, \六十进制计数器_2_nqcc );  // AND_Gate
  and and_4 (and_4_out, CPu_out, Adj0);
  or or_3 (or_3_out, and_3_out, and_4_out);
  Hex_Digit_Display hex_digit_display_3 (.value(ledbase_3_out_5));  // open: dp
  LEDBase ledbase_3 (
    .in_1(\六十进制计数器_1_q1a ), .in_2(\六十进制计数器_1_q1b ), .in_3(\六十进制计数器_1_q1c ), .in_4(\六十进制计数器_1_q1d ),
    .out_5(ledbase_3_out_5));
  Hex_Digit_Display hex_digit_display_4 (.value(ledbase_4_out_5));  // open: dp
  LEDBase ledbase_4 (
    .in_1(\六十进制计数器_1_q0a ), .in_2(\六十进制计数器_1_q0b ), .in_3(\六十进制计数器_1_q0c ), .in_4(\六十进制计数器_1_q0d ),
    .out_5(ledbase_4_out_5));
  \六十进制计数器  \u_六十进制计数器_1  (
    .Clr(Clr), .Adj(Adj0), .Cpu(or_3_out), .Cpd(CPd_out), .nQcc(\六十进制计数器_1_nqcc ), .Q0d(\六十进制计数器_1_q0d ),
    .Q0c(\六十进制计数器_1_q0c ), .Q0b(\六十进制计数器_1_q0b ), .Q0a(\六十进制计数器_1_q0a ), .Q1d(\六十进制计数器_1_q1d ),
    .Q1c(\六十进制计数器_1_q1c ), .Q1b(\六十进制计数器_1_q1b ), .Q1a(\六十进制计数器_1_q1a ));
  LED led_1 (.in(time_report_1_out_13));
  Time_Report time_report_1 (
    .out_13(time_report_1_out_13), .in_1(\六十进制计数器_1_q1d ), .in_2(\六十进制计数器_1_q1c ), .in_3(\六十进制计数器_1_q1b ),
    .in_4(\六十进制计数器_1_q1a ), .in_5(\六十进制计数器_1_q0d ), .in_6(\六十进制计数器_1_q0c ), .in_7(\六十进制计数器_1_q0b ),
    .in_8(\六十进制计数器_1_q0a ), .in_9(\六十进制计数器_2_q1d ), .in_10(\六十进制计数器_2_q1c ), .in_11(\六十进制计数器_2_q1b ),
    .in_12(\六十进制计数器_2_q1a ));
  Clock CP (.out(CP_out));
  Hex_Digit_Display hex_digit_display_5 (.value(ledbase_5_out_5));  // open: dp
  LEDBase ledbase_5 (
    .in_1(\六十进制计数器_2_q1a ), .in_2(\六十进制计数器_2_q1b ), .in_3(\六十进制计数器_2_q1c ), .in_4(\六十进制计数器_2_q1d ),
    .out_5(ledbase_5_out_5));
  Hex_Digit_Display hex_digit_display_6 (.value(ledbase_6_out_5));  // open: dp
  LEDBase ledbase_6 (
    .in_1(\六十进制计数器_2_q0a ), .in_2(\六十进制计数器_2_q0b ), .in_3(\六十进制计数器_2_q0c ), .in_4(\六十进制计数器_2_q0d ),
    .out_5(ledbase_6_out_5));
  \六十进制计数器  \u_六十进制计数器_2  (
    .Clr(Clr), .Adj(1'b0), .Cpu(CP_out), .Cpd(1'b0), .nQcc(\六十进制计数器_2_nqcc ), .Q0d(\六十进制计数器_2_q0d ),
    .Q0c(\六十进制计数器_2_q0c ), .Q0b(\六十进制计数器_2_q0b ), .Q0a(\六十进制计数器_2_q0a ), .Q1d(\六十进制计数器_2_q1d ),
    .Q1c(\六十进制计数器_2_q1c ), .Q1b(\六十进制计数器_2_q1b ), .Q1a(\六十进制计数器_2_q1a ));
endmodule

module \四位二进制可逆计数器  (
  input  CP_U,
  input  CP_D,
  input  nLD,
  input  A,
  input  CLR,
  input  B,
  input  C,
  input  D,
  output Q_A,
  output Q_B,
  output Q_C,
  output Q_D
);

  wire and_1_out, and_2_out, and_3_out, and_4_out, and_5_out, and_6_out, and_7_out, and_8_out, and_9_out,
       and_10_out, and_11_out, and_12_out, and_13_out, and_14_out, d_ff_1_qn, d_ff_2_qn, d_ff_3_qn,
       d_ff_4_qn, not_1_out, not_2_out, not_3_out, or_1_out, or_2_out, or_3_out, or_4_out, or_5_out,
       or_6_out, or_7_out, or_8_out;

  not not_1 (not_1_out, CP_U);
  not not_2 (not_2_out, CP_D);
  not not_3 (not_3_out, nLD);
  or or_1 (or_1_out, not_1_out, not_2_out);
  and and_1 (and_1_out, not_3_out, ~CLR, A);  // AND_Gate
  and and_2 (and_2_out, Q_A, not_1_out);
  and and_3 (and_3_out, d_ff_1_qn, not_2_out);
  and and_4 (and_4_out, not_3_out, ~CLR, B);  // AND_Gate
  and and_5 (and_5_out, Q_A, Q_B, not_1_out);
  and and_6 (and_6_out, d_ff_1_qn, d_ff_2_qn, not_2_out);
  and and_7 (and_7_out, not_3_out, ~CLR, C);  // AND_Gate
  and and_8 (and_8_out, Q_A, Q_B, Q_C, not_1_out);
  and and_9 (and_9_out, d_ff_1_qn, d_ff_2_qn, d_ff_3_qn, not_2_out);
  and and_10 (and_10_out, not_3_out, ~CLR, D);  // AND_Gate
  and and_11 (and_11_out, not_3_out, ~and_1_out);  // AND_Gate
  or or_2 (or_2_out, and_2_out, and_3_out);
  and and_12 (and_12_out, not_3_out, ~and_4_out);  // AND_Gate
  or or_3 (or_3_out, and_5_out, and_6_out);
  and and_13 (and_13_out, not_3_out, ~and_7_out);  // AND_Gate
  or or_4 (or_4_out, and_8_out, and_9_out);
  and and_14 (and_14_out, not_3_out, ~and_10_out);  // AND_Gate
  D_Flip_Flop #(.trigger("falling")) d_ff_1 (
    .clk(or_1_out), .D(d_ff_1_qn), .Q(Q_A), .Qn(d_ff_1_qn), .preset(and_1_out), .reset(or_5_out));
  or or_5 (or_5_out, and_11_out, CLR);
  D_Flip_Flop #(.trigger("falling")) d_ff_2 (
    .clk(or_2_out), .D(d_ff_2_qn), .Q(Q_B), .Qn(d_ff_2_qn), .preset(and_4_out), .reset(or_6_out));
  or or_6 (or_6_out, and_12_out, CLR);
  D_Flip_Flop #(.trigger("falling")) d_ff_3 (
    .clk(or_3_out), .D(d_ff_3_qn), .Q(Q_C), .Qn(d_ff_3_qn), .preset(and_7_out), .reset(or_7_out));
  or or_7 (or_7_out, and_13_out, CLR);
  D_Flip_Flop #(.trigger("falling")) d_ff_4 (
    .clk(or_4_out), .D(d_ff_4_qn), .Q(Q_D), .Qn(d_ff_4_qn), .preset(and_10_out), .reset(or_8_out));
  or or_8 (or_8_out, and_14_out, CLR);
endmodule

module \六十进制计数器  (
  input  Clr,
  input  Adj,
  input  Cpu,
  input  Cpd,
  output Q0d,
  output Q0c,
  output Q0b,
  output Q0a,
  output Q1d,
  output Q1c,
  output Q1b,
  output Q1a,
  output nQcc
);

  wire and_1_out, and_2_out, and_3_out, and_4_out, d_ff_1_qn, nand_1_out, nor_1_out, not_1_out, not_2_out,
       not_3_out, not_4_out, or_1_out, or_2_out, or_3_out, or_4_out, or_5_out, or_6_out;
  wire [3:0] multiplexer_1_out, multiplexer_2_out;

  nand nand_1 (nand_1_out, Adj, Cpd);
  not not_1 (not_1_out, Cpu);
  or or_1 (or_1_out, and_1_out, Clr);
  or or_2 (or_2_out, nand_1_out, nor_1_out);
  nor nor_1 (nor_1_out, or_6_out, or_3_out);
  Multiplexer #(.width(4), .enable("false")) multiplexer_1 (
    .in0(4'b0000), .in1(4'b1001), .out(multiplexer_1_out), .sel(and_2_out));
  or or_3 (or_3_out, Q0d, Q0c, Q0b, Q0a);
  \四位二进制可逆计数器  L (
    .CP_D(or_2_out), .nLD(not_2_out), .A(multiplexer_1_out[0]), .CLR(or_1_out), .B(multiplexer_1_out[1]),
    .C(multiplexer_1_out[2]), .D(multiplexer_1_out[3]), .Q_A(Q0a), .Q_B(Q0b), .Q_C(Q0c), .Q_D(Q0d),
    .CP_U(not_1_out));
  not not_2 (not_2_out, and_2_out);
  and and_1 (and_1_out, Q0d, ~Q0c, Q0b, ~Q0a);  // AND_Gate
  and and_2 (and_2_out, Q0d, Q0c, Q0b, Q0a);
  not not_3 (not_3_out, and_1_out);
  or or_4 (or_4_out, and_3_out, Clr);
  or or_5 (or_5_out, ~or_6_out, ~and_2_out);  // OR_Gate
  or or_6 (or_6_out, Q1d, Q1c, Q1b, Q1a);
  Multiplexer #(.width(4), .enable("false")) multiplexer_2 (
    .in0(4'b0000), .in1(4'b0101), .out(multiplexer_2_out), .sel(and_4_out));
  \四位二进制可逆计数器  H (
    .CP_D(or_5_out), .nLD(not_4_out), .A(multiplexer_2_out[0]), .CLR(or_4_out), .B(multiplexer_2_out[1]),
    .C(multiplexer_2_out[2]), .D(multiplexer_2_out[3]), .Q_A(Q1a), .Q_B(Q1b), .Q_C(Q1c), .Q_D(Q1d),
    .CP_U(not_3_out));
  and and_3 (and_3_out, ~Q1d, Q1c, Q1b, ~Q1a);  // AND_Gate
  and and_4 (and_4_out, Q1d, Q1c, Q1b, Q1a);
  not not_4 (not_4_out, and_4_out);
  and and_5 (nQcc, and_3_out, ~Adj);  // AND_Gate
  D_Flip_Flop #(.trigger("falling")) d_ff_1 (
    .clk(nQcc), .D(d_ff_1_qn), .Qn(d_ff_1_qn), .reset(Clr));  // open: Q, preset
endmodule

module _12_24 (
  input  Clr,
  input  Cpu,
  input  Adj,
  input  Cpd,
  input  Set,
  output out_6,
  output Q1d,
  output Q1c,
  output Q1b,
  output Q1a,
  output Q0d,
  output Q0c,
  output Q0b,
  output Q0a,
  output nQcc
);

  wire and_1_out, and_3_out, and_4_out, d_ff_1_q, d_ff_1_qn, multiplexer_1_out, n12_1_out_7, n12_1_qcc,
       or_1_out;
  wire [3:0] n12_1_i;
  wire [4:0] adder_1_out, and_2_out, n1to5_1_out_2, n1to5_2_out_2, n4to5_1_out_2, subtractor_1_out;

  or or_1 (or_1_out, Cpd, and_4_out);
  mini_d_ff mini_d_ff_1 (.in_1(or_1_out), .out_3(out_6));  // open: in_2
  // Probe on n12_1_i
  _12 u_12_1 (
    .Clr(Clr), .Adj(Adj), .Cpu(Cpu), .Cpd(or_1_out), .i(n12_1_i), .rst_d(and_1_out), .Qcc(n12_1_qcc),
    .out_7(n12_1_out_7));
  and and_1 (and_1_out, or_1_out, and_3_out);
  _4to5 u_4to5_1 (.in_1(n12_1_i), .out_2(n4to5_1_out_2));
  // Probe on n12_1_qcc
  _1to5 u_1to5_1 (.in_1(n12_1_qcc), .out_2(n1to5_1_out_2));
  _1to5 u_1to5_2 (.in_1(Set), .out_2(n1to5_2_out_2));
  assign and_2_out = n1to5_1_out_2 & n1to5_2_out_2 & 5'b01100;  // AND_Gate and_2, 5 bits wide
  and and_3 (and_3_out, n12_1_qcc, n12_1_out_7);
  and and_4 (and_4_out, ~n12_1_qcc, n12_1_out_7);  // AND_Gate
  Adder #(.width(5)) adder_1 (.a(n4to5_1_out_2), .b(and_2_out), .out(adder_1_out), .cin(1'b0));  // open: cout
  // Probe on subtractor_1_out
  _5bits2BCD u_5bits2bcd_1 (
    .e(subtractor_1_out[4]), .h3(Q1d), .d(subtractor_1_out[3]), .h2(Q1c), .c(subtractor_1_out[2]), .h1(Q1b),
    .b(subtractor_1_out[1]), .a(subtractor_1_out[0]), .h0(Q1a), .b3(Q0d), .b2(Q0c), .b1(Q0b), .b0(Q0a));
  Subtractor #(.width(5)) subtractor_1 (
    .a(adder_1_out), .b(5'b00001), .out(subtractor_1_out), .bin(1'b0));  // open: bout
  Multiplexer #(.enable("false")) multiplexer_1 (.in0(n12_1_qcc), .in1(d_ff_1_q), .out(multiplexer_1_out), .sel(Set));
  D_Flip_Flop #(.trigger("falling")) d_ff_1 (
    .clk(n12_1_qcc), .D(d_ff_1_qn), .Q(d_ff_1_q), .Qn(d_ff_1_qn), .preset(Set), .reset(Clr));
  not not_1 (nQcc, multiplexer_1_out);
endmodule

module \六十进制计数器测试电路  (
  input  in_1,
  output out_2
);

  wire button_1_out, button_2_out, clock_1_out, d_ff_1_qn;
  wire [3:0] \六十进制计数器_1_q0a , \六十进制计数器_1_q1a ;

  Clock clock_1 (.out(clock_1_out));
  Button button_1 (.out(button_1_out));
  Hex_Digit_Display hex_digit_display_1 (.value(\六十进制计数器_1_q0a ));  // open: dp
  Hex_Digit_Display hex_digit_display_2 (.value(\六十进制计数器_1_q1a ));  // open: dp
  \六十进制计数器  \u_六十进制计数器_1  (
    .Clr(button_2_out), .Adj(in_1), .Cpu(clock_1_out), .Cpd(button_1_out), .nQcc(out_2),
    .Q0d(\六十进制计数器_1_q0a [3]), .Q0c(\六十进制计数器_1_q0a [2]), .Q0b(\六十进制计数器_1_q0a [1]), .Q0a(\六十进制计数器_1_q0a [0]),
    .Q1d(\六十进制计数器_1_q1a [3]), .Q1c(\六十进制计数器_1_q1a [2]), .Q1b(\六十进制计数器_1_q1a [1]), .Q1a(\六十进制计数器_1_q1a [0]));
  Button button_2 (.out(button_2_out));
  D_Flip_Flop #(.trigger("falling")) d_ff_1 (.clk(out_2), .D(d_ff_1_qn), .Qn(d_ff_1_qn));  // open: Q, preset, reset
endmodule

module AM_PM (
  input  AMPM,
  input  TT,
  output [4:0] out_3,
  output [4:0] out_4,
  output [4:0] out_5,
  output [4:0] out_6
);

  wire [4:0] multiplexer_1_out, multiplexer_2_out;

  Multiplexer #(.width(5), .enable("false")) multiplexer_1 (
    .in0(5'b00001), .in1(5'b10000), .out(multiplexer_1_out), .sel(AMPM));
  Multiplexer #(.width(5), .enable("false")) multiplexer_2 (
    .in0(5'b00101), .in1(5'b10100), .out(multiplexer_2_out), .sel(AMPM));
  assign out_3 = multiplexer_1_out & {5{TT}};  // AND_Gate and_1, 5 bits wide
  assign out_4 = {5{1'b1}} & {5{TT}};  // AND_Gate and_2, 5 bits wide
  assign out_5 = multiplexer_2_out & {5{TT}};  // AND_Gate and_3, 5 bits wide

  assign out_6 = out_3;
endmodule

module AM_PM_Test (
  input  in_1,
  input  in_2
);

  wire [4:0] am_pm_1_out_3, am_pm_1_out_4, am_pm_1_out_5, am_pm_1_out_6;

  DotMatrix #(.matrixcols(4), .matrixrows(5)) dotmatrix_1 (
    .col0(am_pm_1_out_3), .col1(am_pm_1_out_4), .col2(am_pm_1_out_5), .col3(am_pm_1_out_6));
  AM_PM am_pm_1 (
    .AMPM(in_1), .TT(in_2), .out_3(am_pm_1_out_3), .out_4(am_pm_1_out_4), .out_5(am_pm_1_out_5),
    .out_6(am_pm_1_out_6));
endmodule

module Time_Report (
  input  in_1,
  input  in_2,
  input  in_3,
  input  in_4,
  input  in_5,
  input  in_6,
  input  in_7,
  input  in_8,
  input  in_9,
  input  in_10,
  input  in_11,
  input  in_12,
  output out_13
);

  wire and_1_out, and_3_out;

  and and_1 (and_1_out, ~in_1, in_2, ~in_3, in_4, in_5, ~in_6, ~in_7, in_8);  // AND_Gate
  and and_2 (out_13, and_1_out, and_3_out);
  and and_3 (and_3_out, ~in_9, in_10, ~in_11, in_12);  // AND_Gate
endmodule

module _1_8_frequecy_tick (
  input  in_1,
  output out_2
);

  wire d_ff_1_q, d_ff_1_qn, d_ff_2_q, d_ff_2_qn, d_ff_3_q, d_ff_3_qn, d_ff_4_qn;

  D_Flip_Flop #(.trigger("falling")) d_ff_1 (
    .clk(in_1), .D(d_ff_1_qn), .Q(d_ff_1_q), .Qn(d_ff_1_qn));  // open: preset, reset
  D_Flip_Flop #(.trigger("falling")) d_ff_2 (
    .clk(d_ff_1_q), .D(d_ff_2_qn), .Q(d_ff_2_q), .Qn(d_ff_2_qn));  // open: preset, reset
  D_Flip_Flop #(.trigger("falling")) d_ff_3 (
    .clk(d_ff_2_q), .D(d_ff_3_qn), .Q(d_ff_3_q), .Qn(d_ff_3_qn));  // open: preset, reset
  D_Flip_Flop #(.trigger("falling")) d_ff_4 (
    .clk(d_ff_3_q), .D(d_ff_4_qn), .Q(out_2), .Qn(d_ff_4_qn));  // open: preset, reset
endmodule

module _12 (
  input  Adj,
  input  rst_d,
  input  Cpu,
  input  Clr,
  input  Cpd,
  output [3:0] i,
  output out_7,
  output Qcc
);

  wire and_1_out, and_2_out, d_ff_1_qn, nand_1_out, not_1_out, not_2_out, or_1_out, or_2_out;
  wire [3:0] L_q_a, multiplexer_1_out;

  nand nand_1 (nand_1_out, Adj, Cpd);
  not not_1 (not_1_out, Cpu);
  or or_1 (or_1_out, and_1_out, Clr);
  nor nor_1 (out_7, L_q_a[3], L_q_a[2], L_q_a[1], L_q_a[0]);
  Multiplexer #(.width(4), .enable("false")) multiplexer_1 (
    .in0(4'b0000), .in1(4'b1011), .out(multiplexer_1_out), .sel(and_2_out));
  \四位二进制可逆计数器  L (
    .CP_D(nand_1_out), .nLD(not_2_out), .A(multiplexer_1_out[0]), .CLR(or_1_out), .B(multiplexer_1_out[1]),
    .C(multiplexer_1_out[2]), .D(multiplexer_1_out[3]), .Q_A(L_q_a[0]), .Q_B(L_q_a[1]), .Q_C(L_q_a[2]),
    .Q_D(L_q_a[3]), .CP_U(not_1_out));
  // Probe on i
  Adder #(.width(4)) adder_1 (.a(4'b0001), .b(L_q_a), .out(i), .cin(1'b0));  // open: cout
  and and_1 (and_1_out, L_q_a[3], L_q_a[2], ~L_q_a[1], ~L_q_a[0]);  // AND_Gate
  and and_2 (and_2_out, L_q_a[3], L_q_a[2], L_q_a[1], L_q_a[0]);
  not not_2 (not_2_out, and_2_out);
  or or_2 (or_2_out, Clr, rst_d);
  D_Flip_Flop #(.trigger("falling")) d_ff_1 (
    .clk(and_1_out), .D(d_ff_1_qn), .Q(Qcc), .Qn(d_ff_1_qn), .preset(1'b0), .reset(or_2_out));
endmodule

module _4to5 (
  input  [3:0] in_1,
  output [4:0] out_2
);


  assign out_2 = {1'b0, in_1};
endmodule

module _1to5 (
  input  in_1,
  output [4:0] out_2
);


  assign out_2 = {5{in_1}};
endmodule

module _5bits2BCD (
  input  e,
  input  d,
  input  c,
  input  b,
  input  a,
  output h3,
  output h2,
  output h1,
  output h0,
  output b3,
  output b2,
  output b1,
  output b0
);

  wire and_1_out, and_2_out, and_3_out, and_4_out, and_5_out, and_6_out, and_7_out, and_8_out, and_9_out,
       and_10_out, and_11_out, and_12_out, and_13_out, and_14_out, and_15_out, and_16_out, and_17_out,
       and_18_out, not_1_out, not_2_out, not_3_out, not_4_out, not_5_out, not_6_out, not_7_out, not_8_out,
       not_9_out, not_10_out, not_11_out, not_12_out, not_13_out, not_14_out, not_15_out, not_16_out,
       not_17_out, not_18_out, not_19_out, not_20_out, not_21_out, not_22_out, not_23_out, not_24_out,
       not_25_out;

  and and_1 (and_1_out, e, c);
  and and_2 (and_2_out, e, d);
  not not_1 (not_1_out, e);
  not not_2 (not_2_out, e);
  not not_3 (not_3_out, d);
  not not_4 (not_4_out, c);
  not not_5 (not_5_out, e);
  not not_6 (not_6_out, c);
  not not_7 (not_7_out, b);
  not not_8 (not_8_out, d);
  not not_9 (not_9_out, c);
  not not_10 (not_10_out, b);
  not not_11 (not_11_out, e);
  not not_12 (not_12_out, d);
  not not_13 (not_13_out, e);
  not not_14 (not_14_out, c);
  not not_15 (not_15_out, b);
  not not_16 (not_16_out, c);
  not not_17 (not_17_out, e);
  not not_18 (not_18_out, d);
  not not_19 (not_19_out, d);
  not not_20 (not_20_out, e);
  not not_21 (not_21_out, b);
  not not_22 (not_22_out, d);
  not not_23 (not_23_out, c);
  not not_24 (not_24_out, b);
  not not_25 (not_25_out, c);
  or or_1 (h1, and_1_out, and_2_out);
  and and_3 (and_3_out, not_1_out, d, b);
  and and_4 (and_4_out, not_2_out, d, c);
  and and_5 (and_5_out, d, c, b);
  and and_6 (and_6_out, e, not_3_out, not_4_out);
  and and_7 (and_7_out, not_5_out, d, not_6_out, not_7_out);
  and and_8 (and_8_out, e, not_8_out, not_9_out, b);
  and and_9 (and_9_out, e, d, c, not_10_out);
  and and_10 (and_10_out, not_11_out, not_12_out, c);
  and and_11 (and_11_out, not_13_out, c, b);
  and and_12 (and_12_out, e, not_14_out, not_15_out);
  and and_13 (and_13_out, e, d, not_16_out);
  and and_14 (and_14_out, not_17_out, not_18_out, b);
  and and_15 (and_15_out, not_19_out, c, b);
  and and_16 (and_16_out, not_20_out, d, c, not_21_out);
  and and_17 (and_17_out, e, not_22_out, not_23_out, not_24_out);
  and and_18 (and_18_out, e, d, not_25_out, b);
  or or_2 (h0, and_3_out, and_4_out, and_5_out, and_6_out);
  or or_3 (b3, and_7_out, and_8_out, and_9_out);
  or or_4 (b2, and_10_out, and_11_out, and_12_out, and_13_out);
  or or_5 (b1, and_14_out, and_15_out, and_16_out, and_17_out, and_18_out);

  assign b0 = a;
  assign h2 = 1'b0;
  assign h3 = 1'b0;
endmodule

module _5bt2bcdtest (
);

  wire clock_1_out;
  wire [3:0] n5bits2bcd_1_b0, n5bits2bcd_1_h0;
  wire [4:0] counter_1_q;

  Counter #(.width(5), .max('h1f)) counter_1 (
    .Q(counter_1_q), .clk(clock_1_out));  // open: load, D, count, carry, clr, preset, down
  Clock clock_1 (.out(clock_1_out));
  Hex_Digit_Display hex_digit_display_1 (.value(n5bits2bcd_1_h0));  // open: dp
  _5bits2BCD u_5bits2bcd_1 (
    .e(counter_1_q[4]), .h3(n5bits2bcd_1_h0[3]), .d(counter_1_q[3]), .h2(n5bits2bcd_1_h0[2]),
    .c(counter_1_q[2]), .h1(n5bits2bcd_1_h0[1]), .b(counter_1_q[1]), .a(counter_1_q[0]),
    .h0(n5bits2bcd_1_h0[0]), .b3(n5bits2bcd_1_b0[3]), .b2(n5bits2bcd_1_b0[2]), .b1(n5bits2bcd_1_b0[1]),
    .b0(n5bits2bcd_1_b0[0]));
  Hex_Digit_Display hex_digit_display_2 (.value(n5bits2bcd_1_b0));  // open: dp
endmodule

module LEDBase (
  input  in_1,
  input  in_2,
  input  in_3,
  input  in_4,
  output [3:0] out_5
);


  assign out_5 = {in_4, in_3, in_2, in_1};
endmodule

module _12_24_test (
  input  in_1,
  input  in_2
);

  wire button_1_out, clock_1_out, clock_2_out, d_ff_1_qn, n12new_1_out_11, n12new_1_q0a, n12new_1_q0b,
       n12new_1_q0c, n12new_1_q0d, n12new_1_q1a, n12new_1_q1b, n12new_1_q1c, n12new_1_q1d;
  wire [3:0] ledbase_1_out_5, ledbase_2_out_5, n12_1_i;
  wire [4:0] n12new_1_out_6;

  Clock clock_1 (.out(clock_1_out));
  Button button_1 (.out(button_1_out));
  // Probe on n12new_1_out_6
  Hex_Digit_Display hex_digit_display_1 (.value(ledbase_1_out_5), .dp(1'b0));
  LEDBase ledbase_1 (
    .in_1(n12new_1_q1a), .in_2(n12new_1_q1b), .in_3(n12new_1_q1c), .in_4(n12new_1_q1d),
    .out_5(ledbase_1_out_5));
  Hex_Digit_Display hex_digit_display_2 (.value(ledbase_2_out_5), .dp(1'b0));
  LEDBase ledbase_2 (
    .in_1(n12new_1_q0a), .in_2(n12new_1_q0b), .in_3(n12new_1_q0c), .in_4(n12new_1_q0d),
    .out_5(ledbase_2_out_5));
  Clock clock_2 (.out(clock_2_out));
  _12new u_12new_1 (
    .Set(in_2), .Clr(1'b0), .Cpu(clock_1_out), .Adj(1'b1), .Cpd(button_1_out), .Q1d(n12new_1_q1d),
    .Q1c(n12new_1_q1c), .Q1b(n12new_1_q1b), .Q1a(n12new_1_q1a), .out_11(n12new_1_out_11), .Q0d(n12new_1_q0d),
    .Q0c(n12new_1_q0c), .Q0b(n12new_1_q0b), .Q0a(n12new_1_q0a), .out_6(n12new_1_out_6));
  Hex_Digit_Display hex_digit_display_3 (.value(n12_1_i), .dp(1'b0));
  _12 u_12_1 (.Clr(1'b0), .Adj(in_1), .Cpu(clock_2_out), .Cpd(1'b0), .i(n12_1_i), .rst_d(1'b0));  // open: Qcc, out_7
  D_Flip_Flop d_ff_1 (.clk(n12new_1_out_11), .D(d_ff_1_qn), .Qn(d_ff_1_qn));  // open: Q, preset, reset
endmodule

module mini_d_ff (
  input  in_1,
  input  in_2,
  output out_3
);

  wire d_ff_1_qn;

  D_Flip_Flop #(.trigger("falling")) d_ff_1 (
    .clk(in_1), .D(d_ff_1_qn), .Q(out_3), .Qn(d_ff_1_qn), .preset(1'b0), .reset(in_2));
endmodule

module _12new (
  input  Set,
  input  Clr,
  input  Cpu,
  input  Adj,
  input  Cpd,
  output [4:0] out_6,
  output Q1d,
  output Q1c,
  output Q1b,
  output Q1a,
  output out_11,
  output Q0d,
  output Q0c,
  output Q0b,
  output Q0a
);

  wire and_1_out, mini_d_ff_1_out_3, multiplexer_1_out, n12_1_out_7, n12_1_qcc;
  wire [3:0] n12_1_i;
  wire [4:0] adder_1_out, and_2_out, n1to5_1_out_2, n1to5_2_out_2, n4to5_1_out_2;

  // Probe on n12_1_i
  _1to5 u_1to5_1 (.in_1(Set), .out_2(n1to5_1_out_2));
  _1to5 u_1to5_2 (.in_1(n12_1_qcc), .out_2(n1to5_2_out_2));
  _12 u_12_1 (
    .Clr(Clr), .Adj(Adj), .Cpu(Cpu), .Cpd(Cpd), .i(n12_1_i), .rst_d(and_1_out), .Qcc(n12_1_qcc),
    .out_7(n12_1_out_7));
  and and_1 (and_1_out, n12_1_qcc, n12_1_out_7, Cpd);
  _4to5 u_4to5_1 (.in_1(n12_1_i), .out_2(n4to5_1_out_2));
  assign and_2_out = 5'b01100 & n1to5_1_out_2 & n1to5_2_out_2;  // AND_Gate and_2, 5 bits wide
  Multiplexer #(.enable("false")) multiplexer_1 (
    .in0(n12_1_qcc), .in1(mini_d_ff_1_out_3), .out(multiplexer_1_out), .sel(Set));
  mini_d_ff mini_d_ff_1 (.in_1(n12_1_qcc), .out_3(mini_d_ff_1_out_3), .in_2(Clr));
  // Probe on adder_1_out
  Adder #(.width(5)) adder_1 (.a(n4to5_1_out_2), .b(and_2_out), .out(adder_1_out), .cin(1'b0));  // open: cout
  not not_1 (out_11, multiplexer_1_out);
  // Probe on out_6
  _5bits2BCD u_5bits2bcd_1 (
    .e(out_6[4]), .h3(Q1d), .d(out_6[3]), .h2(Q1c), .c(out_6[2]), .h1(Q1b), .b(out_6[1]), .a(out_6[0]),
    .h0(Q1a), .b3(Q0d), .b2(Q0c), .b1(Q0b), .b0(Q0a));
  Subtractor #(.width(5)) subtractor_1 (.a(adder_1_out), .b(5'b00001), .out(out_6), .bin(1'b0));  // open: bout
endmodule

module alarm (
  input  H1d,
  input  H1c,
  input  H1b,
  input  H1a,
  input  [3:0] HH,
  input  H0d,
  input  H0c,
  input  H0b,
  input  H0a,
  input  [3:0] HL,
  input  M1d,
  input  M1c,
  input  M1b,
  input  M1a,
  input  [3:0] MH,
  input  M0d,
  input  M0c,
  input  M0b,
  input  M0a,
  input  [3:0] ML
);

  wire comparator_1_eq, comparator_2_eq, comparator_3_eq, comparator_4_eq;

  Comparator #(.width(4), .mode("unsigned")) comparator_1 (
    .a({H1d, H1c, H1b, H1a}), .b(HH), .eq(comparator_1_eq));  // open: gt, lt
  Comparator #(.width(4), .mode("unsigned")) comparator_2 (
    .a({H0d, H0c, H0b, H0a}), .b(HL), .eq(comparator_2_eq));  // open: gt, lt
  Comparator #(.width(4), .mode("unsigned")) comparator_3 (
    .a({M1d, M1c, M1b, M1a}), .b(MH), .eq(comparator_3_eq));  // open: gt, lt
  Comparator #(.width(4), .mode("unsigned")) comparator_4 (
    .a({M0d, M0c, M0b, M0a}), .b(ML), .eq(comparator_4_eq));  // open: gt, lt
  // AND_Gate and_1 has open pins: in0=comparator_1_eq, in1=comparator_2_eq, in2=comparator_3_eq, in3=comparator_4_eq, out=open
endmodule
